# Fritzing sketch LCDWiring (saved by Fritzing 0.9.3b)
breadboards: 1

parts:
  Part1 = Arduino Uno (Rev3)
  VCC1 = 4 x AAA Battery Mount
  R1 = Resistor [tolerance=±5% resistance=220 package="0805 [SMD]"]
  LCD1 = LCD screen
  R2 = Trimmer Potentiometer [maximum_resistance=10kΩ package=THT]

nets:
  N1: Part1.D11_PWM/MOSI, LCD1.E
  N2: Part1.D12/MISO, LCD1.RS
  N3: Part1.D2, LCD1.DB7
  N4: Part1.D3_PWM, LCD1.DB6
  N5: Part1.D4, LCD1.DB5
  N6: Part1.D5_PWM, LCD1.DB4
  GND: Part1.GND, VCC1.-, LCD1.VSS, LCD1.R/W, LCD1.LED-, R2.leg2
  N7: VCC1.+, R1.Pin_0, LCD1.VDD, R2.leg1
  N8: R1.Pin_1, LCD1.LED+
  N9: LCD1.V0, R2.wiper
